# Fritzing sketch js-1 (saved by Fritzing 0.9.3b)
stripboards: 1

parts:
  Part1 = Arduino Nano (Rev3.0)
  R1 = Resistor [tolerance=±5% resistance=220 package=THT]
  R2 = Resistor [tolerance=±5% resistance=220 package=THT]
  R3 = Resistor [tolerance=±5% resistance=220 package=THT]
  R4 = Resistor [tolerance=±5% resistance=220 package=THT]
  R5 = Resistor [tolerance=±5% resistance=220 package=THT]
  R6 = Resistor [tolerance=±5% resistance=220 package=THT]
  R7 = Resistor [tolerance=±5% resistance=220 package=THT]
  R8 = Resistor [tolerance=±5% resistance=220 package=THT]
  S2 = Toggle Switch [package=THT]
  VCC1 = Battery block 9V
  R9 = Resistor [tolerance=±5% resistance=10k package=THT]
  R10 = Resistor [tolerance=±5% resistance=10k package=THT]
  R11 = Resistor [tolerance=±5% resistance=10k package=THT]
  R12 = Resistor [tolerance=±5% resistance=10k package=THT]
  LED1 = LED - 3mm [color="Red (633nm)" package="3 mm [THT]"]
  LED2 = LED - 3mm [color="Red (633nm)" package="3 mm [THT]"]
  LED3 = LED - 3mm [color="Yellow (595nm)" package="3 mm [THT]"]
  LED4 = LED - 3mm [color="Yellow (595nm)" package="3 mm [THT]"]
  LED5 = LED - 3mm [color="Blue (470nm)" package="3 mm [THT]"]
  LED6 = LED - 3mm [color="Blue (470nm)" package="3 mm [THT]"]
  LED7 = LED - 3mm [color="Green (570nm)" package="3 mm [THT]"]
  LED8 = LED - 3mm [color="Green (570nm)" package="3 mm [THT]"]
  S9 = Pushbutton [package=THT]
  S10 = Pushbutton [package=THT]
  S11 = Pushbutton [package=THT]
  S12 = Pushbutton [package=THT]

nets:
  N1: Part1.D1/TX, Part1.VIN, S2.COM
  N2: Part1.RESET, R12.Pin_0
  N3: Part1.GND, VCC1.-, LED1.cathode, LED2.cathode, LED3.cathode, LED4.cathode, LED5.cathode, LED6.cathode, LED7.cathode, LED8.cathode
  N4: Part1.D2, R1.Pin_0
  N5: Part1.D3, R2.Pin_0
  N6: Part1.D4, R3.Pin_0
  N7: Part1.D5, R4.Pin_0
  N8: Part1.D6, R5.Pin_0
  N9: Part1.D7, R6.Pin_0
  N10: Part1.D8, R7.Pin_0
  N11: Part1.D9, R8.Pin_0
  N12: Part1.5V, S9.leg1, S10.leg1, S11.leg1, S12.leg1
  N13: Part1.A3, R12.Pin_1, S12.leg0
  N14: Part1.A2, R11.Pin_1, S11.leg0
  N15: Part1.A1, R10.Pin_1, S10.leg0
  N16: Part1.A0, R9.Pin_1, S9.leg0
  N17: Part1.AREF, R9.Pin_0, R10.Pin_0, R11.Pin_0
  N18: R1.Pin_1, LED5.anode
  N19: R2.Pin_1, LED6.anode
  N20: R3.Pin_1, LED7.anode
  N21: R4.Pin_1, LED8.anode
  N22: R5.Pin_1, LED3.anode
  N23: R6.Pin_1, LED4.anode
  N24: R7.Pin_1, LED2.anode
  N25: R8.Pin_1, LED1.anode
  N26: S2.L1, VCC1.+
